# Fritzing sketch main (saved by Fritzing 1.0.1rc)
breadboards: 1

parts:
  Grove3 = Grove OLED 128x96
  A3 = Arduino Nano ESP32
  S3 = Momentary Switch [package=ksa_sealed_tac_switch]
  KY-3 = Keyes Relay [package=THT]
  R6 = Resistor [tolerance=±5% resistance=10k package="0402 [SMD]"]
  VCC3 = Battery block 9V
  U4 = Voltage Regulator - 5V [package="DPak [SMD]"]
  M3 = DC Motor [voltage_(max)=6V voltage_(min)=3V]
  Chirp!_Soil_Moisture_Sensor2 = Chirp! Soil Moisture Sensor v2.7.3
  R7 = PHOTOCELL [package=photocell]
  R8 = Resistor [tolerance=±5% resistance=10k package="0402 [SMD]"]

nets:
  GND: Grove3.GND, A3.Pin_14, A3.Pin_19, KY-3.ground, KY-3.NO, R6.Pin_0, VCC3.-, U4.GND, Chirp!_Soil_Moisture_Sensor2.pin_5, R8.Pin_0
  N1: Grove3.VCC, A3.Pin_2, S3.2, Chirp!_Soil_Moisture_Sensor2.Pin_1, R7.P$2
  N2: Grove3.SDA, A3.Pin_8
  N3: Grove3.SCL, A3.Pin_9
  N4: A3.Pin_4, Chirp!_Soil_Moisture_Sensor2.pin_3
  N5: A3.Pin_6, R7.P$1, R8.Pin_1
  N6: A3.Pin_22, S3.3, R6.Pin_1
  N7: A3.Pin_30, KY-3.signal
  N8: KY-3.power, U4.output_voltage, M3.pin_2
  N9: KY-3.C, M3.pin_1
  N10: VCC3.+, U4.input_voltage

notes:
  The actual sensor does not communicate via SPI but returns an analogic value. Consider the "SDA/MOSI" pin as this analog output.
  Water pump
  IN / 5V / GND
  VIN / GND / VOUT
  The Arduino board is
  powered by USB

custom parts:
  Arduino Nano ESP32: Arduino® Nano ESP32 smd.
  Keyes Relay: The Keyes 5V relay module is suitable for SCM development, home appliance control. It uses a 5V~12V TIL control signal which can control DC / AC signal.
