# Fritzing sketch water_level (saved by Fritzing 1.0.1rc)
breadboards: 1

parts:
  A2 = Arduino Nano ESP32
  KY-2 = Keyes Relay [package=THT]
  M2 = DC Motor [voltage_(max)=6V voltage_(min)=3V]
  VCC2 = Battery block 9V
  U3 = Voltage Regulator - 5V [package="DPak [SMD]"]
  S1 = Pushbutton [package="[SMD]"]
  HC-SR04_Sensor_1 = HC-SR04 Ultrasonic Distance Sensor

nets:
  GND: A2.Pin_14, A2.Pin_19, KY-2.ground, KY-2.NO, VCC2.-, U3.GND, HC-SR04_Sensor_1.GND
  N1: A2.Pin_15, VCC2.+, U3.input_voltage
  N2: A2.Pin_20, KY-2.signal
  N3: A2.Pin_22, S1.Pin_3, S1.Pin_4
  N4: A2.Pin_24, HC-SR04_Sensor_1.TRIG
  N5: A2.Pin_26, HC-SR04_Sensor_1.ECHO
  N6: KY-2.power, M2.pin_2, U3.output_voltage, S1.Pin_1, S1.Pin_2, HC-SR04_Sensor_1.VCC
  N7: KY-2.C, M2.pin_1

notes:
  IN / VCC / GND
  VIN / GND / VOUT
  Water Pump
  Distance Sensor (ultrasonic)

custom parts:
  Arduino Nano ESP32: Arduino® Nano ESP32 smd.
  Keyes Relay: The Keyes 5V relay module is suitable for SCM development, home appliance control. It uses a 5V~12V TIL control signal which can control DC / AC signal.
